// Logisim project CPU.circ as structural Verilog: 11 circuits, main circuit main
module main (
);

  FullAdderCasero fulladdercasero_1 ();  // open: A, B, Cin, S, Cout
endmodule

module FullAdderCasero (
  input  A,
  input  B,
  input  Cin,
  output S,
  output Cout
);

  wire and_1_out, and_2_out, xor_1_out;

  xor xor_1 (xor_1_out, A, B);
  Adder adder_1 ();  // open: a, b, out, cin, cout
  xor xor_2 (S, xor_1_out, Cin);
  and and_1 (and_1_out, Cin, xor_1_out);
  and and_2 (and_2_out, B, A);
  or or_1 (Cout, and_1_out, and_2_out);

  // Notes on the sheet:
  //   Full Adder Casero
endmodule

module Sumador (
  input  A7,
  input  A6,
  input  A5,
  input  A4,
  input  A3,
  input  A2,
  input  A1,
  input  A0,
  input  B7,
  input  B6,
  input  B5,
  input  B4,
  input  B3,
  input  B2,
  input  B1,
  input  B0,
  output Cout,
  output S7,
  output S6,
  output S5,
  output S4,
  output S3,
  output S2,
  output S1,
  output S0
);

  wire fulladdercasero_2_cout, fulladdercasero_3_cout, fulladdercasero_4_cout, fulladdercasero_5_cout,
       fulladdercasero_6_cout, fulladdercasero_7_cout, fulladdercasero_8_cout;

  FullAdderCasero fulladdercasero_1 (.A(A7), .B(B7), .Cin(fulladdercasero_2_cout), .S(S7), .Cout(Cout));
  FullAdderCasero fulladdercasero_2 (
    .A(A6), .B(B6), .Cin(fulladdercasero_3_cout), .S(S6), .Cout(fulladdercasero_2_cout));
  FullAdderCasero fulladdercasero_3 (
    .A(A5), .B(B5), .Cin(fulladdercasero_4_cout), .S(S5), .Cout(fulladdercasero_3_cout));
  Adder adder_1 ();  // open: a, b, out, cin, cout
  FullAdderCasero fulladdercasero_4 (
    .A(A4), .B(B4), .Cin(fulladdercasero_5_cout), .S(S4), .Cout(fulladdercasero_4_cout));
  FullAdderCasero fulladdercasero_5 (
    .A(A3), .B(B3), .Cin(fulladdercasero_6_cout), .S(S3), .Cout(fulladdercasero_5_cout));
  FullAdderCasero fulladdercasero_6 (
    .A(A2), .B(B2), .Cin(fulladdercasero_7_cout), .S(S2), .Cout(fulladdercasero_6_cout));
  FullAdderCasero fulladdercasero_7 (
    .A(A1), .B(B1), .Cin(fulladdercasero_8_cout), .S(S1), .Cout(fulladdercasero_7_cout));
  FullAdderCasero fulladdercasero_8 (.A(A0), .B(B0), .Cin(1'b0), .S(S0), .Cout(fulladdercasero_8_cout));

  // Notes on the sheet:
  //   Sumador Casero
endmodule

module Restador (
  input  A7,
  input  A6,
  input  A5,
  input  A4,
  input  A3,
  input  A2,
  input  A1,
  input  A0,
  input  B7,
  input  B6,
  input  B5,
  input  B4,
  input  B3,
  input  B2,
  input  B1,
  input  B0,
  output S7,
  output S6,
  output S5,
  output S4,
  output S3,
  output S2,
  output S1,
  output S0,
  output Cout
);

  wire fulladdercasero_1_cout, fulladdercasero_2_cout, fulladdercasero_3_cout, fulladdercasero_4_cout,
       fulladdercasero_5_cout, fulladdercasero_6_cout, fulladdercasero_7_cout, fulladdercasero_8_cout,
       not_2_out, not_3_out, not_4_out, not_5_out, not_6_out, not_7_out, not_8_out, not_9_out, not_10_out;

  not not_1 (Cout, fulladdercasero_1_cout);
  not not_2 (not_2_out, B7);
  FullAdderCasero fulladdercasero_1 (
    .A(A7), .B(not_2_out), .Cin(fulladdercasero_2_cout), .S(S7), .Cout(fulladdercasero_1_cout));
  not not_3 (not_3_out, B6);
  FullAdderCasero fulladdercasero_2 (
    .A(A6), .B(not_3_out), .Cin(fulladdercasero_3_cout), .S(S6), .Cout(fulladdercasero_2_cout));
  not not_4 (not_4_out, B5);
  FullAdderCasero fulladdercasero_3 (
    .A(A5), .B(not_4_out), .Cin(fulladdercasero_4_cout), .S(S5), .Cout(fulladdercasero_3_cout));
  not not_5 (not_5_out, B4);
  Subtractor subtractor_1 ();  // open: a, b, out, bin, bout
  FullAdderCasero fulladdercasero_4 (
    .A(A4), .B(not_5_out), .Cin(fulladdercasero_5_cout), .S(S4), .Cout(fulladdercasero_4_cout));
  not not_6 (not_6_out, B3);
  FullAdderCasero fulladdercasero_5 (
    .A(A3), .B(not_6_out), .Cin(fulladdercasero_6_cout), .S(S3), .Cout(fulladdercasero_5_cout));
  not not_7 (not_7_out, B2);
  FullAdderCasero fulladdercasero_6 (
    .A(A2), .B(not_7_out), .Cin(fulladdercasero_7_cout), .S(S2), .Cout(fulladdercasero_6_cout));
  not not_8 (not_8_out, B1);
  FullAdderCasero fulladdercasero_7 (
    .A(A1), .B(not_8_out), .Cin(fulladdercasero_8_cout), .S(S1), .Cout(fulladdercasero_7_cout));
  not not_9 (not_9_out, B0);
  not not_10 (not_10_out, 1'b0);
  FullAdderCasero fulladdercasero_8 (.A(A0), .B(not_9_out), .Cin(not_10_out), .S(S0), .Cout(fulladdercasero_8_cout));

  // Notes on the sheet:
  //   Restador Casero
endmodule

module ALU (
  input  A7,
  input  A6,
  input  A5,
  input  A4,
  input  A3,
  input  A2,
  input  A1,
  input  A0,
  input  B7,
  input  B6,
  input  B5,
  input  B4,
  input  B3,
  input  B2,
  input  B1,
  input  B0,
  input  C0,
  input  C1,
  input  C2,
  output Zero,
  output Cout,
  output S7,
  output S6,
  output S5,
  output S4,
  output S3,
  output S2,
  output S1,
  output S0
);

  wire and_1_out, and_2_out, compand_1_s0, compand_1_s1, compand_1_s2, compand_1_s3, compand_1_s4,
       compand_1_s5, compand_1_s6, compand_1_s7, compnand_1_s0, compnand_1_s1, compnand_1_s2, compnand_1_s3,
       compnand_1_s4, compnand_1_s5, compnand_1_s6, compnand_1_s7, compor_1_s0, compor_1_s1, compor_1_s2,
       compor_1_s3, compor_1_s4, compor_1_s5, compor_1_s6, compor_1_s7, compxor_1_s0, compxor_1_s1,
       compxor_1_s2, compxor_1_s3, compxor_1_s4, compxor_1_s5, compxor_1_s6, compxor_1_s7, not_1_out,
       not_2_out, restador_1_cout, restador_1_s0, restador_1_s1, restador_1_s2, restador_1_s3, restador_1_s4,
       restador_1_s5, restador_1_s6, restador_1_s7, sumador_1_cout, sumador_1_s0, sumador_1_s1, sumador_1_s2,
       sumador_1_s3, sumador_1_s4, sumador_1_s5, sumador_1_s6, sumador_1_s7;

  ExactlyOne xor_1 (
    .out(Zero), .in0(A7), .in1(A6), .in2(A5), .in3(A4), .in4(A3), .in5(A2), .in6(A1), .in7(A0),
    .in8(not_1_out), .in9(B7), .in10(B6), .in11(B5), .in12(B4), .in13(B3), .in14(B2), .in15(B1), .in16(B0));
  not not_1 (not_1_out, 1'b0);
  Sumador sumador_1 (
    .B1(B1), .A0(A0), .B0(B0), .A7(A7), .B7(B7), .A6(A6), .B6(B6), .A5(A5), .B5(B5), .A4(A4), .B4(B4),
    .A3(A3), .B3(B3), .A2(A2), .B2(B2), .A1(A1), .S1(sumador_1_s1), .S0(sumador_1_s0), .Cout(sumador_1_cout),
    .S7(sumador_1_s7), .S6(sumador_1_s6), .S5(sumador_1_s5), .S4(sumador_1_s4), .S3(sumador_1_s3),
    .S2(sumador_1_s2));
  Restador restador_1 (
    .B1(B1), .A0(A0), .B0(B0), .A7(A7), .B7(B7), .A6(A6), .B6(B6), .A5(A5), .B5(B5), .A4(A4), .B4(B4),
    .A3(A3), .B3(B3), .A2(A2), .B2(B2), .A1(A1), .S1(restador_1_s1), .S0(restador_1_s0),
    .Cout(restador_1_cout), .S7(restador_1_s7), .S6(restador_1_s6), .S5(restador_1_s5), .S4(restador_1_s4),
    .S3(restador_1_s3), .S2(restador_1_s2));
  CompOR compor_1 (
    .B1(B1), .A0(A0), .B0(B0), .A7(A7), .B7(B7), .A6(A6), .B6(B6), .A5(A5), .B5(B5), .A4(A4), .B4(B4),
    .A3(A3), .B3(B3), .A2(A2), .B2(B2), .A1(A1), .S1(compor_1_s1), .S0(compor_1_s0), .S7(compor_1_s7),
    .S6(compor_1_s6), .S5(compor_1_s5), .S4(compor_1_s4), .S3(compor_1_s3), .S2(compor_1_s2));
  CompAND compand_1 (
    .B1(B1), .A0(A0), .B0(B0), .A7(A7), .B7(B7), .A6(A6), .B6(B6), .A5(A5), .B5(B5), .A4(A4), .B4(B4),
    .A3(A3), .B3(B3), .A2(A2), .B2(B2), .A1(A1), .S1(compand_1_s1), .S0(compand_1_s0), .S7(compand_1_s7),
    .S6(compand_1_s6), .S5(compand_1_s5), .S4(compand_1_s4), .S3(compand_1_s3), .S2(compand_1_s2));
  CompXOR compxor_1 (
    .B1(B1), .A0(A0), .B0(B0), .A7(A7), .B7(B7), .A6(A6), .B6(B6), .A5(A5), .B5(B5), .A4(A4), .B4(B4),
    .A3(A3), .B3(B3), .A2(A2), .B2(B2), .A1(A1), .S1(compxor_1_s1), .S0(compxor_1_s0), .S7(compxor_1_s7),
    .S6(compxor_1_s6), .S5(compxor_1_s5), .S4(compxor_1_s4), .S3(compxor_1_s3), .S2(compxor_1_s2));
  CompNAND compnand_1 (
    .B1(B1), .A0(A0), .B0(B0), .A7(A7), .B7(B7), .A6(A6), .B6(B6), .A5(A5), .B5(B5), .A4(A4), .B4(B4),
    .A3(A3), .B3(B3), .A2(A2), .B2(B2), .A1(A1), .S1(compnand_1_s1), .S0(compnand_1_s0), .S7(compnand_1_s7),
    .S6(compnand_1_s6), .S5(compnand_1_s5), .S4(compnand_1_s4), .S3(compnand_1_s3), .S2(compnand_1_s2));
  not not_2 (not_2_out, C0);
  and and_1 (and_1_out, restador_1_cout, C0);
  or or_1 (Cout, and_1_out, and_2_out);
  Selector selector_1 (
    .E0(sumador_1_s7), .E1(restador_1_s7), .E2(compor_1_s7), .E3(compand_1_s7), .E4(compxor_1_s7),
    .E5(compnand_1_s7), .C2(C0), .C1(C1), .C0(C2), .S(S7));
  Selector selector_2 (
    .E0(sumador_1_s6), .E1(restador_1_s6), .E2(compor_1_s6), .E3(compand_1_s6), .E4(compxor_1_s6),
    .E5(compnand_1_s6), .C2(C0), .C1(C1), .C0(C2), .S(S6));
  Selector selector_3 (
    .E0(sumador_1_s5), .E1(restador_1_s5), .E2(compor_1_s5), .E3(compand_1_s5), .E4(compxor_1_s5),
    .E5(compnand_1_s5), .C2(C0), .C1(C1), .C0(C2), .S(S5));
  Selector selector_4 (
    .E0(sumador_1_s4), .E1(restador_1_s4), .E2(compor_1_s4), .E3(compand_1_s4), .E4(compxor_1_s4),
    .E5(compnand_1_s4), .C2(C0), .C1(C1), .C0(C2), .S(S4));
  Selector selector_5 (
    .E0(sumador_1_s3), .E1(restador_1_s3), .E2(compor_1_s3), .E3(compand_1_s3), .E4(compxor_1_s3),
    .E5(compnand_1_s3), .C2(C0), .C1(C1), .C0(C2), .S(S3));
  Selector selector_6 (
    .E0(sumador_1_s2), .E1(restador_1_s2), .E2(compor_1_s2), .E3(compand_1_s2), .E4(compxor_1_s2),
    .E5(compnand_1_s2), .C2(C0), .C1(C1), .C0(C2), .S(S2));
  Selector selector_7 (
    .E0(sumador_1_s1), .E1(restador_1_s1), .E2(compor_1_s1), .E3(compand_1_s1), .E4(compxor_1_s1),
    .E5(compnand_1_s1), .C2(C0), .C1(C1), .C0(C2), .S(S1));
  Selector selector_8 (
    .E0(sumador_1_s0), .E1(restador_1_s0), .E2(compor_1_s0), .E3(compand_1_s0), .E4(compxor_1_s0),
    .E5(compnand_1_s0), .C2(C0), .C1(C1), .C0(C2), .S(S0));
  and and_2 (and_2_out, sumador_1_cout, not_2_out);

  // Notes on the sheet:
  //   0 Suma
  //   1 Resta
  //   2 OR
endmodule

module CompOR (
  input  A7,
  input  B7,
  input  A6,
  input  B6,
  input  A5,
  input  B5,
  input  A4,
  input  B4,
  input  A3,
  input  B3,
  input  A2,
  input  B2,
  input  A1,
  input  B1,
  input  A0,
  input  B0,
  output S7,
  output S6,
  output S5,
  output S4,
  output S3,
  output S2,
  output S1,
  output S0
);

  or or_1 (S7, A7, B7);
  or or_2 (S6, A6, B6);
  or or_3 (S5, A5, B5);
  or or_4 (S4, A4, B4);
  or or_5 (S3, A3, B3);
  or or_6 (S2, A2, B2);
  or or_7 (S1, A1, B1);
  or or_8 (S0, A0, B0);
endmodule

module CompAND (
  input  A7,
  input  B7,
  input  A6,
  input  B6,
  input  A5,
  input  B5,
  input  A4,
  input  B4,
  input  A3,
  input  B3,
  input  A2,
  input  B2,
  input  A1,
  input  B1,
  input  A0,
  input  B0,
  output S7,
  output S6,
  output S5,
  output S4,
  output S3,
  output S2,
  output S1,
  output S0
);

  and and_1 (S7, A7, B7);
  and and_2 (S6, A6, B6);
  and and_3 (S5, A5, B5);
  and and_4 (S4, A4, B4);
  and and_5 (S3, A3, B3);
  and and_6 (S2, A2, B2);
  and and_7 (S1, A1, B1);
  and and_8 (S0, A0, B0);
endmodule

module CompXOR (
  input  A7,
  input  B7,
  input  A6,
  input  B6,
  input  A5,
  input  B5,
  input  A4,
  input  B4,
  input  A3,
  input  B3,
  input  A2,
  input  B2,
  input  A1,
  input  B1,
  input  A0,
  input  B0,
  output S7,
  output S6,
  output S5,
  output S4,
  output S3,
  output S2,
  output S1,
  output S0
);

  xor xor_1 (S7, A7, B7);
  xor xor_2 (S6, A6, B6);
  xor xor_3 (S5, A5, B5);
  xor xor_4 (S4, A4, B4);
  xor xor_5 (S3, A3, B3);
  xor xor_6 (S2, A2, B2);
  xor xor_7 (S1, A1, B1);
  xor xor_8 (S0, A0, B0);
endmodule

module CompNAND (
  input  A7,
  input  B7,
  input  A6,
  input  B6,
  input  A5,
  input  B5,
  input  A4,
  input  B4,
  input  A3,
  input  B3,
  input  A2,
  input  B2,
  input  A1,
  input  B1,
  input  A0,
  input  B0,
  output S7,
  output S6,
  output S5,
  output S4,
  output S3,
  output S2,
  output S1,
  output S0
);

  nand nand_1 (S7, A7, B7);
  nand nand_2 (S6, A6, B6);
  nand nand_3 (S5, A5, B5);
  nand nand_4 (S4, A4, B4);
  nand nand_5 (S3, A3, B3);
  nand nand_6 (S2, A2, B2);
  nand nand_7 (S1, A1, B1);
  nand nand_8 (S0, A0, B0);
endmodule

module Selector (
  input  C2,
  input  C1,
  input  C0,
  input  E0,
  input  E1,
  input  E2,
  input  E3,
  input  E4,
  input  E5,
  output S
);

  wire and_1_out, and_2_out, and_3_out, and_4_out, and_5_out, and_6_out, and_7_out, and_8_out, not_1_out,
       not_2_out, not_3_out;

  not not_1 (not_1_out, C2);
  not not_2 (not_2_out, C1);
  not not_3 (not_3_out, C0);
  and and_1 (and_1_out, E0, not_3_out, not_2_out, not_1_out);
  and and_2 (and_2_out, E1, C0, not_2_out, not_1_out);
  and and_3 (and_3_out, E2, not_3_out, C1, not_1_out);
  and and_4 (and_4_out, E3, C0, C1, not_1_out);
  and and_5 (and_5_out, E4, not_3_out, not_2_out, C2);
  and and_6 (and_6_out, E5, C0, not_2_out, C2);
  and and_7 (and_7_out, 1'b0, not_3_out, C1, C2);
  and and_8 (and_8_out, 1'b0, C0, C1, C2);
  or or_1 (S, and_1_out, and_2_out, and_3_out, and_4_out, and_5_out, and_6_out);
  // also tied to GND on the sheet: {and_7_out, and_8_out}
endmodule

module CPU (
  input  in_1,
  input  in_2,
  input  in_3,
  input  in_4,
  input  in_5,
  input  in_6,
  input  in_7,
  input  in_8,
  input  in_9,
  input  in_10,
  input  in_11,
  input  in_12,
  input  in_13,
  input  in_14,
  input  in_15,
  input  in_16,
  input  in_17,
  input  in_18,
  input  in_19,
  output out_20,
  output out_21,
  output out_22,
  output out_23,
  output out_24,
  output out_25,
  output out_26,
  output out_27,
  output out_28
);

  wire alu_1_zero;

  ALU alu_1 (
    .B2(in_17), .B1(in_18), .B0(in_19), .C0(in_1), .C1(in_2), .C2(in_3), .A7(in_4), .A6(in_5), .A5(in_6),
    .A4(in_7), .A3(in_8), .A2(in_9), .A1(in_10), .A0(in_11), .B7(in_12), .B6(in_13), .B5(in_14), .B4(in_15),
    .B3(in_16), .Cout(out_20), .S7(out_21), .S6(out_22), .S5(out_23), .S4(out_24), .S3(out_25), .S2(out_26),
    .S1(out_27), .S0(out_28), .Zero(alu_1_zero));
  LED Zero (.in(alu_1_zero));

  // Notes on the sheet:
  //   0 - Sumar
  //   1 - Restar
  //   2 - OR
  //   3 - AND
  //   4 - XOR
  //   5 - NAND
endmodule
